// Logisim project trab SD.circ as structural Verilog: 4 circuits, main circuit main
module main (
  input  [7:0] A,
  input  [7:0] B,
  output [12:0] out_3,
  output [15:0] out_4
);

  wire \multiplicador_mínimo_1_out_7 , \multiplicador_mínimo_2_out_7 , \multiplicador_mínimo_3_out_7 ,
       \multiplicador_mínimo_4_out_7 , \multiplicador_mínimo_5_out_7 , \multiplicador_mínimo_6_out_7 ,
       \multiplicador_mínimo_7_out_7 , \multiplicador_mínimo_9_out_7 , \multiplicador_mínimo_10_out_7 ,
       \multiplicador_mínimo_11_out_7 , \multiplicador_mínimo_12_out_7 , \multiplicador_mínimo_13_out_7 ,
       \multiplicador_mínimo_14_out_7 , \multiplicador_mínimo_15_out_7 , \multiplicador_mínimo_17_out_7 ,
       \multiplicador_mínimo_18_out_7 , \multiplicador_mínimo_19_out_7 , \multiplicador_mínimo_20_out_7 ,
       \multiplicador_mínimo_21_out_7 , \multiplicador_mínimo_22_out_7 , \multiplicador_mínimo_23_out_7 ,
       \multiplicador_mínimo_25_out_7 , \multiplicador_mínimo_26_out_7 , \multiplicador_mínimo_27_out_7 ,
       \multiplicador_mínimo_28_out_7 , \multiplicador_mínimo_29_out_7 , \multiplicador_mínimo_30_out_7 ,
       \multiplicador_mínimo_31_out_7 , somador_completo_1_cout, somador_completo_2_cout,
       somador_completo_3_cout, somador_completo_4_cout, somador_completo_5_cout, somador_completo_6_cout,
       somador_completo_7_cout, somador_completo_8_cout, somador_completo_9_cout, somador_completo_11_cout,
       somador_completo_12_cout, somador_completo_13_cout, somador_completo_14_cout,
       somador_completo_15_cout, somador_completo_16_cout, somador_completo_17_cout,
       somador_completo_18_cout, somador_completo_19_cout;
  wire [9:2] C;
  wire [11:2] D;
  wire [13:6] E;
  wire [15:6] F;

  and and_1 (out_3[0], A[0], B[0]);
  \multiplicador_mínimo  \multiplicador_mínimo_1  (
    .in_3(A[1]), .in_4(A[0]), .in_5(B[1]), .out_6(out_3[1]), .in_1(1'b0),
    .out_7(\multiplicador_mínimo_1_out_7 ), .in_2(B[0]));
  \multiplicador_mínimo  \multiplicador_mínimo_2  (
    .in_3(A[2]), .in_4(A[1]), .in_5(B[1]), .out_6(C[2]), .in_1(\multiplicador_mínimo_1_out_7 ),
    .out_7(\multiplicador_mínimo_2_out_7 ), .in_2(B[0]));
  \multiplicador_mínimo  \multiplicador_mínimo_3  (
    .in_3(A[3]), .in_4(A[2]), .in_5(B[1]), .out_6(C[3]), .in_1(\multiplicador_mínimo_2_out_7 ),
    .out_7(\multiplicador_mínimo_3_out_7 ), .in_2(B[0]));
  \multiplicador_mínimo  \multiplicador_mínimo_4  (
    .in_3(A[4]), .in_4(A[3]), .in_5(B[1]), .out_6(C[4]), .in_1(\multiplicador_mínimo_3_out_7 ),
    .out_7(\multiplicador_mínimo_4_out_7 ), .in_2(B[0]));
  \multiplicador_mínimo  \multiplicador_mínimo_5  (
    .in_3(A[5]), .in_4(A[4]), .in_5(B[1]), .out_6(C[5]), .in_1(\multiplicador_mínimo_4_out_7 ),
    .out_7(\multiplicador_mínimo_5_out_7 ), .in_2(B[0]));
  \multiplicador_mínimo  \multiplicador_mínimo_6  (
    .in_3(A[6]), .in_4(A[5]), .in_5(B[1]), .out_6(C[6]), .in_1(\multiplicador_mínimo_5_out_7 ),
    .out_7(\multiplicador_mínimo_6_out_7 ), .in_2(B[0]));
  \multiplicador_mínimo  \multiplicador_mínimo_7  (
    .in_3(A[7]), .in_4(A[6]), .in_5(B[1]), .out_6(C[7]), .in_1(\multiplicador_mínimo_6_out_7 ),
    .out_7(\multiplicador_mínimo_7_out_7 ), .in_2(B[0]));
  \multiplicador_mínimo  \multiplicador_mínimo_8  (
    .in_3(A[6]), .in_4(1'b0), .in_5(1'b0), .out_6(C[8]), .in_1(\multiplicador_mínimo_7_out_7 ), .out_7(C[9]),
    .in_2(B[0]));
  and and_2 (D[2], A[0], B[2]);
  \multiplicador_mínimo  \multiplicador_mínimo_9  (
    .in_3(A[1]), .in_4(A[0]), .in_5(B[3]), .out_6(D[3]), .in_1(1'b0), .out_7(\multiplicador_mínimo_9_out_7 ),
    .in_2(B[2]));
  \multiplicador_mínimo  \multiplicador_mínimo_10  (
    .in_3(A[2]), .in_4(A[1]), .in_5(B[3]), .out_6(D[4]), .in_1(\multiplicador_mínimo_9_out_7 ),
    .out_7(\multiplicador_mínimo_10_out_7 ), .in_2(B[2]));
  \multiplicador_mínimo  \multiplicador_mínimo_11  (
    .in_3(A[3]), .in_4(A[2]), .in_5(B[3]), .out_6(D[5]), .in_1(\multiplicador_mínimo_10_out_7 ),
    .out_7(\multiplicador_mínimo_11_out_7 ), .in_2(B[2]));
  \multiplicador_mínimo  \multiplicador_mínimo_12  (
    .in_3(A[4]), .in_4(A[3]), .in_5(B[3]), .out_6(D[6]), .in_1(\multiplicador_mínimo_11_out_7 ),
    .out_7(\multiplicador_mínimo_12_out_7 ), .in_2(B[2]));
  \multiplicador_mínimo  \multiplicador_mínimo_13  (
    .in_3(A[5]), .in_4(A[4]), .in_5(B[3]), .out_6(D[7]), .in_1(\multiplicador_mínimo_12_out_7 ),
    .out_7(\multiplicador_mínimo_13_out_7 ), .in_2(B[2]));
  \multiplicador_mínimo  \multiplicador_mínimo_14  (
    .in_3(A[6]), .in_4(A[5]), .in_5(B[3]), .out_6(D[8]), .in_1(\multiplicador_mínimo_13_out_7 ),
    .out_7(\multiplicador_mínimo_14_out_7 ), .in_2(B[2]));
  \multiplicador_mínimo  \multiplicador_mínimo_15  (
    .in_3(A[7]), .in_4(A[6]), .in_5(B[3]), .out_6(D[9]), .in_1(\multiplicador_mínimo_14_out_7 ),
    .out_7(\multiplicador_mínimo_15_out_7 ), .in_2(B[2]));
  \multiplicador_mínimo  \multiplicador_mínimo_16  (
    .in_3(A[6]), .in_4(1'b0), .in_5(1'b0), .out_6(D[10]), .in_1(\multiplicador_mínimo_15_out_7 ),
    .out_7(D[11]), .in_2(B[2]));
  and and_3 (out_4[4], A[0], B[4]);
  \multiplicador_mínimo  \multiplicador_mínimo_17  (
    .in_3(A[1]), .in_4(A[0]), .in_5(B[5]), .out_6(out_4[5]), .in_1(1'b0),
    .out_7(\multiplicador_mínimo_17_out_7 ), .in_2(B[4]));
  \multiplicador_mínimo  \multiplicador_mínimo_18  (
    .in_3(A[2]), .in_4(A[1]), .in_5(B[5]), .out_6(E[6]), .in_1(\multiplicador_mínimo_17_out_7 ),
    .out_7(\multiplicador_mínimo_18_out_7 ), .in_2(B[4]));
  \multiplicador_mínimo  \multiplicador_mínimo_19  (
    .in_3(A[3]), .in_4(A[2]), .in_5(B[5]), .out_6(E[7]), .in_1(\multiplicador_mínimo_18_out_7 ),
    .out_7(\multiplicador_mínimo_19_out_7 ), .in_2(B[4]));
  \multiplicador_mínimo  \multiplicador_mínimo_20  (
    .in_3(A[4]), .in_4(A[3]), .in_5(B[5]), .out_6(E[8]), .in_1(\multiplicador_mínimo_19_out_7 ),
    .out_7(\multiplicador_mínimo_20_out_7 ), .in_2(B[4]));
  \multiplicador_mínimo  \multiplicador_mínimo_21  (
    .in_3(A[5]), .in_4(A[4]), .in_5(B[5]), .out_6(E[9]), .in_1(\multiplicador_mínimo_20_out_7 ),
    .out_7(\multiplicador_mínimo_21_out_7 ), .in_2(B[4]));
  \multiplicador_mínimo  \multiplicador_mínimo_22  (
    .in_3(A[6]), .in_4(A[5]), .in_5(B[5]), .out_6(E[10]), .in_1(\multiplicador_mínimo_21_out_7 ),
    .out_7(\multiplicador_mínimo_22_out_7 ), .in_2(B[4]));
  \multiplicador_mínimo  \multiplicador_mínimo_23  (
    .in_3(A[7]), .in_4(A[6]), .in_5(B[5]), .out_6(E[11]), .in_1(\multiplicador_mínimo_22_out_7 ),
    .out_7(\multiplicador_mínimo_23_out_7 ), .in_2(B[4]));
  \multiplicador_mínimo  \multiplicador_mínimo_24  (
    .in_3(A[6]), .in_4(1'b0), .in_5(1'b0), .out_6(E[12]), .in_1(\multiplicador_mínimo_23_out_7 ),
    .out_7(E[13]), .in_2(B[4]));
  and and_4 (F[6], A[0], B[6]);
  \multiplicador_mínimo  \multiplicador_mínimo_25  (
    .in_3(A[1]), .in_4(A[0]), .in_5(B[7]), .out_6(F[7]), .in_1(1'b0),
    .out_7(\multiplicador_mínimo_25_out_7 ), .in_2(B[6]));
  \multiplicador_mínimo  \multiplicador_mínimo_26  (
    .in_3(A[2]), .in_4(A[1]), .in_5(B[7]), .out_6(F[8]), .in_1(\multiplicador_mínimo_25_out_7 ),
    .out_7(\multiplicador_mínimo_26_out_7 ), .in_2(B[6]));
  \multiplicador_mínimo  \multiplicador_mínimo_27  (
    .in_3(A[3]), .in_4(A[2]), .in_5(B[7]), .out_6(F[9]), .in_1(\multiplicador_mínimo_26_out_7 ),
    .out_7(\multiplicador_mínimo_27_out_7 ), .in_2(B[6]));
  \multiplicador_mínimo  \multiplicador_mínimo_28  (
    .in_3(A[4]), .in_4(A[3]), .in_5(B[7]), .out_6(F[10]), .in_1(\multiplicador_mínimo_27_out_7 ),
    .out_7(\multiplicador_mínimo_28_out_7 ), .in_2(B[6]));
  \multiplicador_mínimo  \multiplicador_mínimo_29  (
    .in_3(A[5]), .in_4(A[4]), .in_5(B[7]), .out_6(F[11]), .in_1(\multiplicador_mínimo_28_out_7 ),
    .out_7(\multiplicador_mínimo_29_out_7 ), .in_2(B[6]));
  \multiplicador_mínimo  \multiplicador_mínimo_30  (
    .in_3(A[6]), .in_4(A[5]), .in_5(B[7]), .out_6(F[12]), .in_1(\multiplicador_mínimo_29_out_7 ),
    .out_7(\multiplicador_mínimo_30_out_7 ), .in_2(B[6]));
  \multiplicador_mínimo  \multiplicador_mínimo_31  (
    .in_3(A[7]), .in_4(A[6]), .in_5(B[7]), .out_6(F[13]), .in_1(\multiplicador_mínimo_30_out_7 ),
    .out_7(\multiplicador_mínimo_31_out_7 ), .in_2(B[6]));
  \multiplicador_mínimo  \multiplicador_mínimo_32  (
    .in_3(A[6]), .in_4(1'b0), .in_5(1'b0), .out_6(F[14]), .in_1(\multiplicador_mínimo_31_out_7 ),
    .out_7(F[15]), .in_2(B[6]));
  somador_completo somador_completo_1 (.Cin(1'b0), .A(C[2]), .B(D[2]), .S(out_3[2]), .Cout(somador_completo_1_cout));
  somador_completo somador_completo_2 (
    .Cin(somador_completo_1_cout), .A(C[3]), .B(D[3]), .S(out_3[3]), .Cout(somador_completo_2_cout));
  somador_completo somador_completo_3 (
    .Cin(somador_completo_2_cout), .A(C[4]), .B(D[4]), .S(out_3[4]), .Cout(somador_completo_3_cout));
  somador_completo somador_completo_4 (
    .Cin(somador_completo_3_cout), .A(C[5]), .B(D[5]), .S(out_3[5]), .Cout(somador_completo_4_cout));
  somador_completo somador_completo_5 (
    .Cin(somador_completo_4_cout), .A(C[6]), .B(D[6]), .S(out_3[6]), .Cout(somador_completo_5_cout));
  somador_completo somador_completo_6 (
    .Cin(somador_completo_5_cout), .A(C[7]), .B(D[7]), .S(out_3[7]), .Cout(somador_completo_6_cout));
  somador_completo somador_completo_7 (
    .Cin(somador_completo_6_cout), .A(C[8]), .B(D[8]), .S(out_3[8]), .Cout(somador_completo_7_cout));
  somador_completo somador_completo_8 (
    .Cin(somador_completo_7_cout), .A(C[9]), .B(D[9]), .S(out_3[9]), .Cout(somador_completo_8_cout));
  somador_completo somador_completo_9 (
    .Cin(somador_completo_8_cout), .A(1'b0), .B(D[10]), .S(out_3[10]), .Cout(somador_completo_9_cout));
  somador_completo somador_completo_10 (
    .Cin(somador_completo_9_cout), .A(1'b0), .B(D[11]), .S(out_3[11]), .Cout(out_3[12]));
  somador_completo somador_completo_11 (.Cin(1'b0), .A(E[6]), .B(F[6]), .S(out_4[6]), .Cout(somador_completo_11_cout));
  somador_completo somador_completo_12 (
    .Cin(somador_completo_11_cout), .A(E[7]), .B(F[7]), .S(out_4[7]), .Cout(somador_completo_12_cout));
  somador_completo somador_completo_13 (
    .Cin(somador_completo_12_cout), .A(E[8]), .B(F[8]), .S(out_4[8]), .Cout(somador_completo_13_cout));
  somador_completo somador_completo_14 (
    .Cin(somador_completo_13_cout), .A(E[9]), .B(F[9]), .S(out_4[9]), .Cout(somador_completo_14_cout));
  somador_completo somador_completo_15 (
    .Cin(somador_completo_14_cout), .A(E[10]), .B(F[10]), .S(out_4[10]), .Cout(somador_completo_15_cout));
  somador_completo somador_completo_16 (
    .Cin(somador_completo_15_cout), .A(E[11]), .B(F[11]), .S(out_4[11]), .Cout(somador_completo_16_cout));
  somador_completo somador_completo_17 (
    .Cin(somador_completo_16_cout), .A(E[12]), .B(F[12]), .S(out_4[12]), .Cout(somador_completo_17_cout));
  somador_completo somador_completo_18 (
    .Cin(somador_completo_17_cout), .A(E[13]), .B(F[13]), .S(out_4[13]), .Cout(somador_completo_18_cout));
  somador_completo somador_completo_19 (
    .Cin(somador_completo_18_cout), .A(1'b0), .B(F[14]), .S(out_4[14]), .Cout(somador_completo_19_cout));
  somador_completo somador_completo_20 (
    .Cin(somador_completo_19_cout), .A(1'b0), .B(F[15]), .S(out_4[15]));  // open: Cout

  assign out_4[3:0] = 4'b0000;

  // Other names for the same wires on the sheet: C[1:0] = out_3[1:0]; c0 = out_3[0]; G[12:0] = out_3; g0 = out_3[0];
  //   c1 = out_3[1]; g1 = out_3[1]; g2 = out_3[2]; g3 = out_3[3]; g4 = out_3[4]; g5 = out_3[5]; g6 = out_3[6];
  //   g7 = out_3[7]; g8 = out_3[8]; g9 = out_3[9]; g10 = out_3[10]; g11 = out_3[11]; g12 = out_3[12];
  //   E[5:4] = out_4[5:4]; e4 = out_4[4]; H[15:4] = out_4[15:4]; h4 = out_4[4]; e5 = out_4[5]; h5 = out_4[5];
  //   h6 = out_4[6]; h7 = out_4[7]; h8 = out_4[8]; h9 = out_4[9]; h10 = out_4[10]; h11 = out_4[11]; h12 = out_4[12];
  //   h13 = out_4[13]; h14 = out_4[14]; h15 = out_4[15]
endmodule

module meio_somador (
  input  A,
  input  B,
  output S,
  output Cout
);

  xor xor_1 (S, A, B);
  and and_1 (Cout, A, B);
endmodule

module somador_completo (
  input  Cin,
  input  A,
  input  B,
  output S,
  output Cout
);

  wire MS_2_cout, MS_2_s, MS_cout;

  meio_somador MS (.A(Cin), .B(MS_2_s), .S(S), .Cout(MS_cout));
  meio_somador MS_2 (.A(A), .B(B), .S(MS_2_s), .Cout(MS_2_cout));
  or or_1 (Cout, MS_cout, MS_2_cout);
endmodule

module \multiplicador_mínimo  (
  input  in_1,
  input  in_2,
  input  in_3,
  input  in_4,
  input  in_5,
  output out_6,
  output out_7
);

  wire and_1_out, and_2_out;

  and and_1 (and_1_out, in_2, in_3);
  and and_2 (and_2_out, in_4, in_5);
  somador_completo somador_completo_1 (.Cin(in_1), .A(and_1_out), .B(and_2_out), .S(out_6), .Cout(out_7));
endmodule
